# Fritzing sketch fluffbug_v3.0 (saved by Fritzing 0.9.5d)
circuit board: 5.08cm x 5.48602cm
breadboards: 1

parts:
  J1 = female pin header, 12 pins [form="♀ (female)"]
  J2 = female pin header, 16 pins [form="♀ (female)"]
  X1 = USB Connectors [package=usb-microb]
  - = female pin header, 1 pin [form="♀ (female)"]
  + = female pin header, 1 pin [form="♀ (female)"]
  X2 = SWITCH_SPDT [package=kps-1290]
  U1 = QFN-32 [chip_label=SAMD21 package=QFN]
  Pad2 = Pad [width=2.4 height=2.4 connect=center]
  C1 = Ceramic Capacitor [capacitance=1µF package="0603 [SMD, multilayer]"]
  C2 = Ceramic Capacitor [capacitance=1µF package="0603 [SMD, multilayer]"]
  S4 = mystery part, 3 pins [chip_label=Servo]
  S3 = mystery part, 3 pins [chip_label=Servo]
  U3 = SO08 [chip_label=SWD7 package=SO]
  R1 = Resistor [tolerance=±5% resistance=220 package="0603 [SMD]"]
  Pad20 = Pad [width=3.81 height=2.4 connect=center]
  S6 = mystery part, 3 pins [chip_label=Servo]
  S5 = mystery part, 3 pins [chip_label=Servo]
  S7 = mystery part, 3 pins [chip_label=Servo]
  S0 = mystery part, 3 pins [chip_label=Servo]
  D1 = Rectifier Diode [package="Melf DO-213 AA [SMD]"]
  D2 = Rectifier Diode [package="Melf DO-213 AA [SMD]"]
  U4 = MCP73831T-2ACIOT Lithium Charger IC [package=sot23-5]
  D3 = smd LED [color="Orange (605nm)" package="0603 [SMD]"]
  R2 = Resistor [tolerance=±5% resistance=1k package="0603 [SMD]"]
  R3 = Resistor [tolerance=±5% resistance=1k package="0603 [SMD]"]
  C3 = Ceramic Capacitor [capacitance=10µF package="0603 [SMD, multilayer]"]
  U2 = Voltage Regulator [package=sot23-5]
  S1 = mystery part, 3 pins [chip_label=Servo]
  S2 = mystery part, 3 pins [chip_label=Servo]
  X4 = Buzzer 7.5mm [package=buzzer-hyg7525]
  R4 = Resistor [tolerance=±5% resistance=220 package="0603 [SMD]"]
  OUT_G_3V = female pin header, 3 pins [form="♀ (female)"]

nets:
  VBAT: J1.pin1, X2.S, S4.pin2, S3.pin2, S6.pin2, S5.pin2, S7.pin2, S0.pin2, D1.anode, S1.pin2, S2.pin2
  EN: J1.pin2
  VBUS: J1.pin3, X1.VBUS, D2.anode, U4.VDD
  D13: J1.pin4, U1.18
  D12: J1.pin5, U1.20
  D11: J1.pin6, U1.17
  D10: J1.pin7, U1.19
  D9: J1.pin8, U1.15
  D6: J1.pin9, U1.25
  D5: J1.pin10, U1.4
  SCL: J1.pin11, U1.22
  SDA: J1.pin12, U1.21
  D1: J2.pin2, U1.11
  D0: J2.pin3, U1.12
  MISO: J2.pin4, U1.31
  MOSI: J2.pin5, U1.1
  SCK: J2.pin6, U1.32
  A5/S6: J2.pin7, U1.13, S5.pin3
  A4/S3: J2.pin8, U1.8, S7.pin3
  A3/S2: J2.pin9, U1.6, S4.pin3
  A2/S0: J2.pin10, U1.5, S0.pin3
  A1/S4: J2.pin11, U1.2, S2.pin3
  A0: J2.pin12, U1.3, R4.Pin_1
  GND: J2.pin13, X1.GND, U1.10, U1.28, Pad2.pad, C1.0, C2.0, S4.pin1, S3.pin1, U3.1, U3.2, U3.3, U3.4, S6.pin1, S5.pin1, S7.pin1, S0.pin1, U4.VSS, R2.Pin_1, U2.GND, S1.pin1, S2.pin1, X4.-, OUT_G_3V.pin2
  AREF: J2.pin14
  3.3V: J2.pin15, U1.9, U1.30, C2.1, U2.OUT, OUT_G_3V.pin3
  NRST: J2.pin16, U1.26
  D+: X1.D+, U1.24
  D-: X1.D-, U1.23
  N1: -.pin1, U3.5, U3.7, U3.8, Pad20.pad, C3.0
  N2: +.pin1, X2.P, R1.Pin_1, C3.1
  N3: X2.O, U4.VBAT, D3.anode
  S1: U1.7, S6.pin3
  S5: U1.14, S3.pin3
  S7: U1.16, S1.pin3
  IR: U1.27, OUT_G_3V.pin1
  N4: U1.29, C1.1
  N5: U3.6, R1.Pin_0
  N6: D1.cathode, D2.cathode, U2.IN, U2.EN
  N7: U4.STAT, R3.Pin_1
  N8: U4.PROG, R2.Pin_0
  N9: D3.cathode, R3.Pin_0
  N10: X4.+, R4.Pin_0

notes:
  BAT X USB 13 12 11 10 9  6 5 SCL SDA
  RS 3V X GND A0 A1 A2 A3 A4 A5 SCK MO MI RX TX X
  FluffBug v3.0
  0N .. 0FF

custom parts:
  Buzzer 7.5mm: buzzer 7.5mm
