# Fritzing sketch fluffbug_v4.0 (saved by Fritzing 0.9.5d)
breadboards: 1

parts:
  - = female pin header, 1 pin [form="♀ (female)"]
  + = female pin header, 1 pin [form="♀ (female)"]
  X2 = SWITCH_SPDT [package=kps-1290]
  U1 = SO08 [chip_label=SWD7 package=SO]
  R1 = Resistor [tolerance=±5% resistance=220 package="0603 [SMD]"]
  Pad20 = Pad [width=3.81 height=2.4 connect=center]  # not connected
  U2 = MCP73831T-2ACIOT Lithium Charger IC [package=sot23-5]
  D2 = smd LED [color="Orange (605nm)" package="0603 [SMD]"]
  R2 = Resistor [tolerance=±5% resistance=1k package="0603 [SMD]"]
  R3 = Resistor [tolerance=±5% resistance=1k package="0603 [SMD]"]
  C1 = Ceramic Capacitor [capacitance=10µF package="0603 [SMD, multilayer]"]
  X1 = Buzzer 7.5mm [package=buzzer-hyg7525]
  R4 = Resistor [tolerance=±5% resistance=220 package="0603 [SMD]"]
  J1 = double row female pin header, 16 pins [form="♀ (female)"]  # not connected
  J2 = double row female pin header, 16 pins [form="♀ (female)"]  # not connected
  J4 = double row female pin header, 12 pins [form="♀ (female)"]  # not connected
  J3 = double row female pin header, 12 pins [form="♀ (female)"]  # not connected
  D1 = smd LED [color="Orange (605nm)" package="0805 [SMD]"]
  J5 = double row female pin header, 12 pins [form="♀ (female)"]  # not connected
  C2 = Ceramic Capacitor [capacitance=10µF package="0603 [SMD, multilayer]"]  # not connected

nets:
  N1: -.pin1, U1.5, U1.7, U1.8, C1.0
  N2: +.pin1, X2.P, R1.Pin_1, U2.VBAT, C1.1
  VSERVO: X2.S, D1.anode
  GND: U1.1, U1.2, U1.3, U1.4, U2.VSS, R2.Pin_1, X1.-
  N3: U1.6, R1.Pin_0
  N4: U2.STAT, R3.Pin_1
  VBUS: U2.VDD, D2.anode, D1.cathode
  N5: U2.PROG, R2.Pin_0
  N6: D2.cathode, R3.Pin_0
  N7: X1.+, R4.Pin_0
  A0: R4.Pin_1

notes:
  FluffBug v4.0
  0N / 0FF

custom parts:
  Buzzer 7.5mm: buzzer 7.5mm
