# Fritzing sketch fluffbug_v1.0 (saved by Fritzing 0.9.4)
circuit board: 5.08cm x 5.48602cm
breadboards: 1

parts:
  J1 = female pin header, 12 pins [form="♀ (female)"]
  J2 = female pin header, 16 pins [form="♀ (female)"]
  X1 = USB Connectors [package=usb-microb]
  - = female pin header, 1 pin [form="♀ (female)"]
  + = female pin header, 1 pin [form="♀ (female)"]
  ON = SWITCH_SPDT [package=kps-1290]
  U1 = QFN-32 [chip_label=SAMD21 package=QFN]
  Pad2 = Pad [width=2.4 height=2.4 connect=center]
  C1 = Ceramic Capacitor [capacitance=1µF package="0603 [SMD, multilayer]"]
  C2 = Ceramic Capacitor [capacitance=1µF package="0603 [SMD, multilayer]"]
  S2 = mystery part, 3 pins [chip_label=Servo]
  S0 = mystery part, 3 pins [chip_label=Servo]
  S3 = mystery part, 3 pins [chip_label=Servo]
  S1 = mystery part, 3 pins [chip_label=Servo]
  U3 = SO08 [chip_label=SWD7 package=SO]
  R1 = Resistor [tolerance=±5% resistance=220 package="0603 [SMD]"]
  Pad20 = Pad [width=3.81 height=2.4 connect=center]
  U2 = Voltage Regulator [package=sot23-5]
  S6 = mystery part, 3 pins [chip_label=Servo]
  S7 = mystery part, 3 pins [chip_label=Servo]
  S5 = mystery part, 3 pins [chip_label=Servo]
  S4 = mystery part, 3 pins [chip_label=Servo]
  D1 = Rectifier Diode [package="Melf DO-213 AA [SMD]"]
  D2 = Rectifier Diode [package="Melf DO-213 AA [SMD]"]
  U4 = MCP73831T-2ACIOT Lithium Charger IC [package=sot23-5]
  CHARGE = smd LED [color="Orange (605nm)" package="0603 [SMD]"]
  R2 = Resistor [tolerance=±5% resistance=1k package="0603 [SMD]"]
  R3 = Resistor [tolerance=±5% resistance=330 package="0603 [SMD]"]
  U5 = PAM8391 [part_number=PAM8301AAF package=SOT23-6]
  R5 = Resistor [tolerance=±10% resistance=51k package="0603 [SMD]"]
  R4 = Resistor [tolerance=±10% resistance=4.7k package="0603 [SMD]"]
  C5 = Ceramic Capacitor [capacitance=0.1µF package="0603 [SMD, multilayer]"]
  Pad22 = Pad [width=2.54 height=5.08 connect=center]
  speaker2 = Pad [width=2.54 height=5.08 connect=center]
  C6 = Ceramic Capacitor [capacitance=10µF package="0805 [SMD, multilayer]"]

nets:
  VBAT: J1.pin1, ON.O, S2.pin2, S0.pin2, S3.pin2, S1.pin2, R1.Pin_1, S6.pin2, S7.pin2, S5.pin2, S4.pin2, D1.anode, U5.VDD, C6.1
  EN: J1.pin2
  VBUS: J1.pin3, X1.VBUS, D2.anode, U4.VDD, CHARGE.anode
  D13: J1.pin4, U1.18
  D12: J1.pin5, U1.20
  D11: J1.pin6, U1.17
  D10: J1.pin7, U1.19
  D9: J1.pin8, U1.15
  D6: J1.pin9, U1.25
  D5: J1.pin10, U1.4
  SCL: J1.pin11, U1.22
  SDA: J1.pin12, U1.21
  D4: J2.pin1
  D1: J2.pin2, U1.11
  D0: J2.pin3, U1.12
  MISO: J2.pin4, U1.32
  MOSI: J2.pin5, U1.1
  SCK: J2.pin6, U1.31
  A5: J2.pin7
  A4: J2.pin8
  A3: J2.pin9
  A2: J2.pin10
  A1: J2.pin11
  A0: J2.pin12, U1.3, R4.Pin_1
  GND: J2.pin13, X1.GND, U1.10, U1.28, Pad2.pad, C1.0, C2.0, S2.pin1, S0.pin1, S3.pin1, S1.pin1, U3.1, U3.2, U3.3, U3.4, U2.GND, S6.pin1, S7.pin1, S5.pin1, S4.pin1, U4.VSS, R2.Pin_1, U5.GND, R5.Pin_0, C6.0
  AREF: J2.pin14
  3.3V: J2.pin15, U1.9, U1.30, C2.1, U2.OUT
  NRST: J2.pin16, U1.26
  D+: X1.D+, U1.24
  D-: X1.D-, U1.23
  N1: -.pin1, U3.5, U3.7, U3.8, Pad20.pad
  N2: +.pin1, ON.P
  N3: ON.S, U4.VBAT
  S4: U1.2, S4.pin3
  S0: U1.5, S0.pin3
  S2: U1.6, S2.pin3
  S1: U1.7, S1.pin3
  S3: U1.8, S3.pin3
  S6: U1.13, S6.pin3
  S5: U1.14, S5.pin3
  S7: U1.16, S7.pin3
  MUTE: U1.27, U5.!SD, R5.Pin_1
  N4: U1.29, C1.1
  N5: U3.6, R1.Pin_0
  N6: U2.IN, U2.EN, D1.cathode, D2.cathode
  N7: U4.STAT, R3.Pin_1
  N8: U4.PROG, R2.Pin_0
  N9: CHARGE.cathode, R3.Pin_0
  N10: U5.OUT+, speaker2.pad
  N11: U5.IN, C5.1
  N12: U5.OUT-, Pad22.pad
  N13: R4.Pin_0, C5.0

notes:
  BAT X USB 13 12 11 10 9 6 5 SCL SDA
  RST 3V X GND A0 X  X X  X  X SCK MO MI RX TX X
  FluffBug v1.0
