# Fritzing sketch leg (saved by Fritzing 0.9.3b)
circuit board: 6.27324cm x 2.03315cm
breadboards: 1

parts:
  Pad1 = Pad [width=2.5 height=1.7 connect=center]
  Pad2 = Pad [width=2.5 height=1.7 connect=center]
  J1 = female pin header, 2 pins [form="♀ (female)"]
  Pad3 = Pad [width=2.5 height=1.7 connect=center]
  Pad4 = Pad [width=2.5 height=1.7 connect=center]

nets:
  N1: Pad1.pad, J1.pin2, Pad4.pad
  N2: Pad2.pad, J1.pin1, Pad3.pad
